# Fritzing sketch JaBoire (saved by Fritzing 0.9.2b)
breadboards: 1

parts:
  Part1 = Arduino Uno (Rev3)
  J1 = Piezo Speaker
  R1 = Resistor [tolerance=±5% resistance=220 package=THT]
  R2 = Resistor [tolerance=±5% resistance=220 package=THT]
  S1 = Pushbutton [package="[THT]"]

nets:
  N1: Part1.A1, J1.pin1, R2.Pin_1
  N2: Part1.A5/SCL, R1.Pin_1, S1.Pin_3, S1.Pin_4
  N3: Part1.5V, J1.pin2, S1.Pin_1, S1.Pin_2
  N4: Part1.GND, R1.Pin_0, R2.Pin_0
